# Fritzing sketch CarDuino2018 (saved by Fritzing 0.9.3b)
breadboards: 1

parts:
  M1 = ESC [part_number="ESC F05428 - 10A"]
  920KV_Motor1 = DJI 920 KV Motor [part_number="Nikko Motor 540"]
  Power_plug2 = Power plug  # not connected
  Composant1 = Arduino Mega 2560 (Rev3)
  J1 = Basic Servo [part_number=MG995]
  BAT1 = LIPO-1000mAh [package=lipo-1000]  # not connected
  BAT2 = Battery Holders [package=lipo-1100mAh]

nets:
  N1: M1.U, 920KV_Motor1.u
  N2: M1.V, 920KV_Motor1.v
  N3: M1.W, 920KV_Motor1.w
  N4: M1.DATA, Composant1.D9_PWM
  GND: M1.GND, Composant1.GND, J1.gnd, BAT2.-
  N5: Composant1.D10_PWM, J1.pulse
  N6: J1.vcc, BAT2.+

custom parts:
  DJI 920 KV Motor: DJI Brushless Outrunner 2212/920K Motor F330-550
