# Fritzing sketch CarDuino2020 (saved by Fritzing 0.9.3b)
breadboards: 2

parts:
  M1 = ESC [part_number="ESC F05428 - 10A"]
  920KV_Motor1 = DJI 920 KV Motor [part_number="Nikko Motor 540"]
  Composant1 = Arduino Mega 2560 (Rev3)
  J1 = Basic Servo [part_number=MG995]
  BAT1 = LIPO-1000mAh [package=lipo-1000]
  BAT2 = Battery Holders [package=lipo-1100mAh]
  S1 = Toggle Switch [package=THT]
  S2 = Toggle Switch [package=THT]
  D1 = Diode [package=diode-1n4148]
  U1 = Voltage Regulator -- 3.3 V -- LM1117
  Composant4 = NRF24L01+ Breakout Board
  R1 = Resistor [tolerance=±5% resistance=10k package="0805 [SMD]"]
  R2 = Resistor [tolerance=±5% resistance=10k package="0805 [SMD]"]
  R3 = Resistor [tolerance=±5% resistance=10k package="0805 [SMD]"]
  R4 = Resistor [tolerance=±5% resistance=10k package="0805 [SMD]"]
  C3 = Electrolytic Capacitor [capacitance=10μF package="0605 [SMD, electrolytic]"]
  C4 = Electrolytic Capacitor [capacitance=10μF package="0605 [SMD, electrolytic]"]
  ESP32_-_Back1 = ESP32 - CAM
  J2 = Basic Servo [part_number=MG995]
  J3 = Basic Servo [part_number=MG995]
  U2 = Voltage Regulator -- 5 V -- LM1117
  D2 = Diode [package=diode-1n4148]
  D3 = Diode [package=diode-1n4148]
  D4 = Diode [package=diode-1n4148]

nets:
  N1: M1.U, 920KV_Motor1.u
  N2: M1.W, 920KV_Motor1.w
  N3: M1.DATA, Composant1.D9_PWM
  N4: M1.GND, D1.A
  N5: Composant1.A0, R3.Pin_1, R4.Pin_1
  N6: Composant1.A1, R1.Pin_0, R2.Pin_0
  N7: Composant1.D10_PWM, J1.pulse
  N8: Composant1.D8_PWM, Composant4.CS
  GND: Composant1.GND, J1.gnd, S1.L2, D1.C, U1.GND, Composant4.GND, R1.Pin_1, R2.Pin_1, R4.Pin_0, C3.-, C4.-, ESP32_-_Back1.GND, D3.C, D4.C
  VIN: Composant1.VIN, BAT2.+, U1.IN, ESP32_-_Back1.5V
  N9: Composant1.D5_PWM, J3.pulse
  N10: Composant1.D6_PWM, J2.pulse
  N11: Composant1.D7_PWM, Composant4.CE
  N12: Composant1.D50, Composant4.MISO
  N13: Composant1.D51, Composant4.MOSI
  N14: Composant1.D52, Composant4.SCK
  N15: J1.vcc, R3.Pin_0, C3.+, C4.+, U2.IN
  N16: BAT1.+, S2.L1
  N17: BAT2.-, S1.COM
  N18: U1.OUT, Composant4.VCC
  N19: J2.gnd, D4.A
  VCC: J2.vcc, J3.vcc, U2.OUT, D2.C
  N20: J3.gnd, D3.A
  N21: U2.GND, D2.A

custom parts:
  DJI 920 KV Motor: DJI Brushless Outrunner 2212/920K Motor F330-550
  Voltage Regulator -- 3.3 V -- LM1117: LM1117-3.3 Voltage regulator, 3.3 V output. Note that the pinout order is not the same as LM7805 or LM7833.
  ESP32 - CAM: The ESP32-CAM has a very competitive small-size camera module that can operate independently as a minimum system with a footprint of only 27*40.5*4.5mm and a deep sleep current of up to 6mA.
  Voltage Regulator -- 5 V -- LM1117: LM1117-3.3 Voltage regulator, 5 V output. Note that the pinout order is not the same as LM7805 or LM7833.
