# Fritzing sketch CarDuino_old (saved by Fritzing 0.9.3b)
breadboards: 3

parts:
  S3 = H-Bridge with L298N
  VCC2 = 4 x AAA Battery Mount
  S4 = Toggle Switch [package=THT]
  M2 = DC Motor
  R2 = Resistor [tolerance=±5% resistance=100 package="0603 [SMD]"]
  R3 = Resistor [tolerance=±5% resistance=100 package="0603 [SMD]"]
  R4 = Resistor [tolerance=±5% resistance=100 package="0603 [SMD]"]
  R5 = Resistor [tolerance=±5% resistance=100 package="0603 [SMD]"]
  LED12 = smd LED [color="Red (633nm)" package="0603 [SMD]"]
  LED13 = smd LED [color="Red (633nm)" package="0603 [SMD]"]
  Composant4 = Arduino Mega 2560 (Rev3)
  Composant5 = Bluetooth Module Breakout - Roving Networks (RN-41)
  Q1 = NPN-Transistor [package="TO92 [THT]"]
  M3 = DC Motor [part_number=gatling]
  R6 = Resistor [tolerance=±5% resistance=22 package="0603 [SMD]"]
  J2 = Basic Servo
  J3 = Basic Servo
  U7 = LCD-16X2 [package=lcd-16x2_noholes]
  S5 = Momentary Switch [package=ksa_sealed_tac_switch]
  R8 = Resistor [tolerance=±5% resistance=220 package="0603 [SMD]"]
  R9 = Resistor [tolerance=±5% resistance=10k package="0603 [SMD]"]
  R10 = Resistor [tolerance=±5% resistance=2.2k package="0603 [SMD]"]
  J4 = Basic Servo
  J5 = Piezo Speaker
  LED14 = smd LED [color="Yellow (595nm)" package="0603 [SMD]"]
  LED15 = smd LED [color="Yellow (595nm)" package="0603 [SMD]"]
  LED16 = smd LED [color="White (4500K)" package="0603 [SMD]"]
  LED17 = smd LED [color="White (4500K)" package="0603 [SMD]"]
  LED18 = smd LED [color="White (4500K)" package="0603 [SMD]"]
  LED19 = smd LED [color="White (4500K)" package="0603 [SMD]"]
  LED20 = smd LED [color="White (4500K)" package="0603 [SMD]"]
  LED21 = smd LED [color="White (4500K)" package="0603 [SMD]"]
  U8 = RF24G Header [package=rf24g-2x5]
  R11 = Resistor [tolerance=±5% resistance=220 package="0603 [SMD]"]
  R12 = Resistor [tolerance=±5% resistance=220 package="0603 [SMD]"]
  U9 = Battery Holders [package=lipo-1100mAh]
  U5 = Battery Holders [package=lipo-1100mAh]

nets:
  N1: S3.12V, U5.+
  GND: S3.GND, VCC2.+, S4.COM, LED12.cathode, LED13.cathode, Composant4.GND, Composant5.GND, Q1.C, J2.gnd, J3.gnd, U7.VSS, U7.R_W, U7.K, R9.Pin_1, R10.Pin_1, J4.gnd, J5.pin1, LED14.cathode, LED15.cathode, U8.CLK2, U5.-
  5V: S3.5V, Composant4.5V, Composant5.VCC, R6.Pin_1, U7.VDD, S5.1, J5.pin2
  N2: S3.IN3, Composant4.D8_PWM
  N3: S3.IN4, Composant4.D7_PWM
  N4: S3.ENB, Composant4.D9_PWM
  N5: S3.M1-01, M2.pin_2
  N6: S3.M1-02, M2.pin_1
  N7: VCC2.-, S4.L1, U9.-
  N8: R2.Pin_0, R3.Pin_0, R4.Pin_0, Composant4.D24
  N9: R2.Pin_1, LED20.anode, LED21.anode
  N10: R3.Pin_1, LED18.anode, LED19.anode
  N11: R4.Pin_1, LED16.anode, LED17.anode
  N12: R5.Pin_0, Composant4.D25
  N13: R5.Pin_1, LED12.anode, LED13.anode
  N14: Composant4.A15, R8.Pin_0
  N15: Composant4.D19/RX1, Composant5.UARTRX
  N16: Composant4.D18/TX1, Composant5.UARTTX
  N17: Composant4.D12_PWM, J4.pulse
  N18: Composant4.D11_PWM, J2.pulse
  N19: Composant4.D10_PWM, J3.pulse
  N20: Composant4.D22, Q1.E
  N21: Composant4.D26, R12.Pin_0
  N22: Composant4.D27, R11.Pin_0
  N23: Composant4.D45, U7.DB7
  N24: Composant4.D46, U7.DB6
  N25: Composant4.D47, U7.DB5
  N26: Composant4.D48, U7.DB4
  N27: Composant4.D49, U7.E
  N28: Composant4.D50, U7.RS
  N29: Composant4.D51, S5.4
  N30: Q1.B, M3.pin_2
  N31: M3.pin_1, R6.Pin_0
  VCC: J2.vcc, J3.vcc, J4.vcc, U9.+
  N32: U7.VO, R10.Pin_0
  N33: U7.A, R8.Pin_1
  N34: S5.3, R9.Pin_0
  N35: LED14.anode, R12.Pin_1
  N36: LED15.anode, R11.Pin_1
  N37: LED16.cathode, U8.CE
  N38: LED17.cathode, U8.GND
  N39: LED18.cathode, U8.CS
  N40: LED19.cathode, U8.CLK1
  N41: LED20.cathode, U8.DATA
  N42: LED21.cathode, U8.DR1

custom parts:
  H-Bridge with L298N: h-bridge

// code stored in the sketch: NikkoCarduino.ino
#include "Arduino.h"
#include "enum_lights.h"
#include <Wire.h>
#include <LiquidCrystal.h>
#include <Servo.h>
#include <SimpleTimer.h>
//#include <NewTone.h>
#define DEBUG false
/*******************************************************************************************************************************************************/
/*          PIN LAYOUT        */
/*******************************************************************************************************************************************************/
const int BUZZER_PIN = 2;

const int ESC_PIN = 7;

const int DIRECTION_PIN = 10;
const int TURRET_PAN_PIN = 11;
const int TURRET_TILT_PIN = 12;
const int FIRING_PIN = 22;

const int PIN_LIGHTS_FRONT = 24;
const int PIN_LIGHTS_TOP = 24;
const int PIN_LIGHTS_BACK = 25;
const int RIGHT_LIGHT_PIN = 26;
const int LEFT_LIGHT_PIN = 27;

LiquidCrystal lcd(50, 49, 48, 47, 46, 45);
const int LCD_TOGGLE_BUTTON = 51;
const int LCD_LIGHT_PIN = A15;

/*******************************************************************************************************************************************************/
/*          Direction - MG995 Servo        */
/*******************************************************************************************************************************************************/

Servo dirServo;

const int SERVO_LIMIT_MIN = 30;
const int SERVO_CENTER    = 75;
const int SERVO_LIMIT_MAX = 120;
//const int DIRECTION_PIN = 10;

int servoPosition = 0;
void Servo_setup() {
  dirServo.attach(DIRECTION_PIN);
  dirServo.write(SERVO_CENTER);
  servoPosition = SERVO_CENTER;
	turning_lights_setup();
}


void turn(int joyY) {
  int val = SERVO_CENTER;
  if(joyY<-50){
    val = SERVO_LIMIT_MIN;
  }else{
    if(joyY<-10){
      val = (SERVO_CENTER - SERVO_LIMIT_MIN)/2 + SERVO_LIMIT_MIN;
    }else{
      if(joyY<10){
        val = SERVO_CENTER;
      }else{
        if(joyY<50){
          val = (SERVO_LIMIT_MAX - SERVO_CENTER)/2 + SERVO_CENTER;
        }else{
          val = SERVO_LIMIT_MAX;
        }
      }
    }
  }  
  if (abs(servoPosition - val) > 5) {
    dirServo.write(val);
    servoPosition = val;
  }
}

void turn_analog(int joyY) {
  int val = map(joyY, -100, 100, SERVO_LIMIT_MIN, SERVO_LIMIT_MAX);
  Serial.println("turn");
  Serial.println(servoPosition - val);
  if (abs(servoPosition - val) > 5) {
    dirServo.write(val);
    servoPosition = val;
  }
}
void test_SERVO() {
  delay(1000);
  dirServo.write(SERVO_LIMIT_MIN);
  delay(1000);
  dirServo.write(SERVO_LIMIT_MAX);
  delay(1000);
  dirServo.write(SERVO_CENTER);
}

/*******************************************************************************************************************************************************/
/*          Turning lights + buzzer          */
/*******************************************************************************************************************************************************/
//const int LEFT_LIGHT_PIN = 27;
//const int RIGHT_LIGHT_PIN = 26;
//const int BUZZER_PIN = 2;
const int BUZZER_SOUND_1 = 160;
const int BUZZER_SOUND_2 = 40;
const int BUZZER_SOUND_LENGTH = 20;
SimpleTimer timer;

int leftTimerId = 0;
int rightTimerId = 0;
void turning_lights_setup() {
	pinMode(LEFT_LIGHT_PIN, OUTPUT);
	pinMode(RIGHT_LIGHT_PIN, OUTPUT);
  rightTimerId = timer.setInterval(500, blinkRight);
  timer.disable(rightTimerId);
  leftTimerId = timer.setInterval(500, blinkLeft);
  timer.disable(leftTimerId);
}
int state = 0;
void light_turn(int joyX){
   if(joyX>5){
    if(state!=-1){
    	digitalWrite(LEFT_LIGHT_PIN, LOW);
    	timer.disable(leftTimerId);
      timer.enable(rightTimerId);
      state = -1;
    }
  }else{
    if(joyX<-5){
      if(state!=1){
  	    digitalWrite(RIGHT_LIGHT_PIN, LOW);
	      timer.disable(rightTimerId);
        timer.enable(leftTimerId);
        state = 1;
      }
    }else{
      digitalWrite(LEFT_LIGHT_PIN, LOW);
      digitalWrite(RIGHT_LIGHT_PIN, LOW);
      timer.disable(rightTimerId);
      timer.disable(leftTimerId);
      state = 0;
    }
  }
  timer.run(); 
}

volatile int leftState = LOW;
void blinkLeft(){
Serial.println("******************************BLINKLEFT*****************************************");
  leftState = !leftState;
  digitalWrite(LEFT_LIGHT_PIN, leftState);
	turnSound(leftState);
}

volatile int rightState = LOW;
void blinkRight(){
Serial.println("******************************BLINKRIGHT*****************************************");
  rightState = !rightState;
  digitalWrite(RIGHT_LIGHT_PIN, rightState);
	turnSound(rightState);
}

void turnSound(int state){
	if(state==HIGH){
		tone(BUZZER_PIN,BUZZER_SOUND_1,BUZZER_SOUND_LENGTH);
//		NewTone(BUZZER_PIN,BUZZER_SOUND_1,BUZZER_SOUND_LENGTH);
	}else{
		tone(BUZZER_PIN,BUZZER_SOUND_2,BUZZER_SOUND_LENGTH);
//		NewTone(BUZZER_PIN,BUZZER_SOUND_2,BUZZER_SOUND_LENGTH);
	}
}

/*******************************************************************************************************************************************************/
/*          Turret - MG995 Servo          */
/*******************************************************************************************************************************************************/

Servo turretServoPan; //hori
//const int TURRET_PAN_PIN = 11;
int posPanTurret = 90;
const int minPosPanTurret = 5;
const int maxPosPanTurret = 175;
const int speedPanTurret = 10;

Servo turretServoTilt; //vert
//const int TURRET_TILT_PIN = 12;
int posTiltTurret = 90;
const int minPosTiltTurret = 90;
const int maxPosTiltTurret = 160;
const int speedTiltTurret = 5;

//const int FIRING_PIN = 22;
int ammo = 6;

void Turret_setup() {
  pinMode(FIRING_PIN, OUTPUT);
  turretServoTilt.attach(TURRET_TILT_PIN);
  turretServoTilt.write(posTiltTurret);
  turretServoPan.attach(TURRET_PAN_PIN);
  turretServoPan.write(posPanTurret);
}

void turnTurret(int joyX, int joyY) {
  Serial.print("pos pan:");
  Serial.print(posPanTurret);
  Serial.print(" pos tilt:");
  Serial.println(posTiltTurret);
  
  //Horizontal
  if (joyX < -30 && posPanTurret <= maxPosPanTurret-speedPanTurret) {
    posPanTurret = posPanTurret + map(joyX, 0, -100, 0, speedPanTurret);
    turretServoPan.write(posPanTurret);
  } else if (joyX > 30 && posPanTurret >= minPosPanTurret+speedPanTurret) {
    posPanTurret = posPanTurret - map(joyX, 0, 100, 0, speedPanTurret);
    turretServoPan.write(posPanTurret);
  }
  //Vertical
  if (joyY < -30 && posTiltTurret <= maxPosTiltTurret-speedTiltTurret) {
    posTiltTurret = posTiltTurret + map(joyY, 0, -100, 0, speedTiltTurret);
    turretServoTilt.write(posTiltTurret);
  } else if (joyY > 30 && posTiltTurret >= minPosTiltTurret+speedTiltTurret) {
    posTiltTurret = posTiltTurret - map(joyY, 0, 100, 0, speedTiltTurret);;
    turretServoTilt.write(posTiltTurret);
  }
}

void fire() {
  if (ammo > 0) {
    ammo--;
    digitalWrite(FIRING_PIN, HIGH);
    delay(100);
    digitalWrite(FIRING_PIN, LOW);
  }
}
void fireAll() {
  digitalWrite(FIRING_PIN, HIGH);
  delay(600);
  digitalWrite(FIRING_PIN, LOW);
}
void reload() {
  ammo = 6;
}
int getAmmoLeft() {
  return ammo;
}
String getAmmoStatus() {
  return "Ammo: " + String(ammo);
}

/*******************************************************************************************************************************************************/
/*          Nikko Motor  with ESC F05428        */
/*******************************************************************************************************************************************************/
const int ESC_MIN = 27;
const int ESC_MAX = 144;
//const int ESC_PIN = 7;
Servo escServo;

void Motor_setup() {
	escServo.attach(ESC_PIN);
}

int move(int joyY) {
  int speed = map(joyY, -100, 100 , ESC_MIN, ESC_MAX);
  escServo.write(speed);
}




/*******************************************************************************************************************************************************/
/*          LCD        */
/*******************************************************************************************************************************************************/
// initialize the library with the numbers of the interface pins
//LiquidCrystal lcd(50, 49, 48, 47, 46, 45);
//const int LCD_TOGGLE_BUTTON = 51;
//const int LCD_LIGHT_PIN = A15;

int lcdState = HIGH;         // the current state of the output pin
int buttonState;             // the current reading from the input pin
int lastButtonState = LOW;   // the previous reading from the input pin

// the following variables are long's because the time, measured in miliseconds,
// will quickly become a bigger number than can be stored in an int.
long lastDebounceTime = 0;  // the last time the output pin was toggled
long debounceDelay = 50;    // the debounce time; increase if the output flickers

void LCD_setup() {
  pinMode(LCD_TOGGLE_BUTTON, INPUT);
  pinMode(LCD_LIGHT_PIN, OUTPUT);
  digitalWrite(LCD_LIGHT_PIN, HIGH);
  // set up the LCD's number of columns and rows:
  lcd.begin(16, 2);
  // Print a message to the LCD.
  lcd.print("CARDUINO");
}
void LCD_toggle(){
  // read the state of the switch into a local variable:
  int reading = digitalRead(LCD_TOGGLE_BUTTON);

  // check to see if you just pressed the button
  // (i.e. the input went from LOW to HIGH),  and you've waited
  // long enough since the last press to ignore any noise:

  // If the switch changed, due to noise or pressing:
  if (reading != lastButtonState) {
    // reset the debouncing timer
    lastDebounceTime = millis();
  }

  if ((millis() - lastDebounceTime) > debounceDelay) {
    // whatever the reading is at, it's been there for longer
    // than the debounce delay, so take it as the actual current state:

    // if the button state has changed:
    if (reading != buttonState) {
      buttonState = reading;

      // only toggle the LED if the new button state is HIGH
      if (buttonState == HIGH) {
        lcdState = !lcdState;
        if(lcdState){
          lcd.display();
          digitalWrite(LCD_LIGHT_PIN, HIGH);
        }else{
          lcd.noDisplay();    
          digitalWrite(LCD_LIGHT_PIN, LOW);
        }        
      }
    }
  }

  // save the reading.  Next time through the loop,
  // it'll be the lastButtonState:
  lastButtonState = reading;  
}


/*******************************************************************************************************************************************************/
/*          Lights        */
/*******************************************************************************************************************************************************/
//const int PIN_LIGHTS_FRONT = 24;
//const int PIN_LIGHTS_TOP = 24;
//const int PIN_LIGHTS_BACK = 25;

void Lights_setup() {
  pinMode(PIN_LIGHTS_FRONT, OUTPUT);
  pinMode(PIN_LIGHTS_TOP, OUTPUT);
  pinMode(PIN_LIGHTS_BACK, OUTPUT);
}

void lightUp(LIGHTS light, int highLow) {
  switch (light) {
    case LIGHTS_FRONT:
      digitalWrite(PIN_LIGHTS_FRONT, highLow);
      break;
    case LIGHTS_TOP:
      digitalWrite(PIN_LIGHTS_TOP, highLow);
      break;
    case LIGHTS_BACK:
      digitalWrite(PIN_LIGHTS_BACK, highLow);
      break;
  }
}
void turnOffAllLights() {
  lightUp(LIGHTS_FRONT, LOW);
  lightUp(LIGHTS_TOP, LOW);
  lightUp(LIGHTS_BACK, LOW);
}
void turnOnAllLights() {
  lightUp(LIGHTS_FRONT, HIGH);
  lightUp(LIGHTS_TOP, HIGH);
  lightUp(LIGHTS_BACK, HIGH);
}

void testLights() {
  lightUp(LIGHTS_FRONT, HIGH);
  delay(5000);
  turnOffAllLights();
  delay(1000);
  lightUp(LIGHTS_TOP, HIGH);
  delay(5000);
  turnOffAllLights();
  delay(1000);
  lightUp(LIGHTS_BACK, HIGH);
  delay(5000);
  turnOffAllLights();
  delay(1000);
  turnOnAllLights();
  delay(1000);
  turnOnAllLights();
  delay(1000);
  turnOnAllLights();
  delay(1000);
}
/*******************************************************************************************************************************************************/




#define VERSION     "\n\nAndroTest V2.0 - @kas2014\ndemo for V5.X App (6 button version)"

// V2.0  changed to pure ASCII Communication Protocol ** not backward compatible **
// V1.4  improved communication errors handling
// V1.3  renamed for publishing, posted on 09/05/2014
// V1.2  Text display   ** not backward compatible **
// V1.1  Integer display
// V1.0  6 buttons + 4 data char implemented

// Demo setup:
// Button #1 controls pin #13 LED
// Button #4 toggle datafield display rate
// Button #5 configured as "push" button (momentary)
// Other buttons display demo message

// Arduino pin#2 to TX BlueTooth module
// Arduino pin#3 to RX BlueTooth module
// make sure your BT board is set @57600 bps
// better remove SoftSerial for PWM based projects

// For Mega 2560:
// remove   #include "SoftwareSerial.h", SoftwareSerial mySerial(2,3);
// search/replace  mySerial  >> Serial1
// pin#18 to RX bluetooth module, pin#19 to TX bluetooth module


#define    STX          0x02
#define    ETX          0x03
#define    SLOW         750                            // Datafields refresh rate (ms)
#define    FAST         250                             // Datafields refresh rate (ms)

//SoftwareSerial mySerial(18, 19);                          // BlueTooth module: pin#2=TX pin#3=RX
byte cmd[8] = {0, 0, 0, 0, 0, 0, 0, 0};                 // bytes received
byte buttonStatus = 0;                                  // first Byte sent to Android device
long previousMillis = 0;                                // will store last time Buttons status was updated
long sendInterval = SLOW;                               // interval between Buttons status transmission (milliseconds)
String displayStatus = "xxxx";                          // message to Android device
boolean directionAxe = true;
boolean connected = false;

void setup()  {
  Serial.begin(9600);
  Serial1.begin(57600);
  Motor_setup();
  Servo_setup();
  Turret_setup();
  Lights_setup();
  LCD_setup();
	turning_lights_setup();

  lcd.setCursor(0, 1);
  lcd.print("Wait connection...");
  connected = false;
  Serial.println(VERSION);
  test_SERVO();
  while (Serial1.available())  Serial1.read();        // empty RX buffer
}

void loop() {
  if (Serial1.available())  {                          // data received from smartphone
    delay(2);
    cmd[0] =  Serial1.read();
    if (cmd[0] == STX)  {
      int i = 1;
      while (Serial1.available())  {
        delay(1);
        cmd[i] = Serial1.read();
        if (cmd[i] > 127 || i > 7)                 break; // Communication error
        if ((cmd[i] == ETX) && (i == 2 || i == 7))   break; // Button or Joystick data
        i++;
      }
      if     (i == 2) {
        getButtonState(cmd[1]);    // 3 Bytes  ex: < STX "C" ETX >
      } else if (i == 7) {
        getJoystickState(cmd);     // 6 Bytes  ex: < STX "200" "180" ETX >
      }
    }
    if (connected == false) {
      lcd.setCursor(0, 1);
      lcd.print("Connected       ");
      connected = true;
    }
  }
  //sendBlueToothData();
	LCD_toggle();
}


void sendBlueToothData()  {
  static long previousMillis = 0;
  long currentMillis = millis();
  if (currentMillis - previousMillis > sendInterval) {  // send data back to smartphone
    previousMillis = currentMillis;

    // Data frame transmitted back from Arduino to Android device:
    // < 0X02   Buttons state   0X01   DataField#1   0x04   DataField#2   0x05   DataField#3    0x03 >
    // < 0X02      "01011"      0X01     "120.00"    0x04     "-4500"     0x05  "Motor enabled" 0x03 >    // example

    Serial1.print((char)STX);                                             // Start of Transmission
    Serial1.print(getButtonStatusString());  Serial1.print((char)0x1);   // buttons status feedback
    Serial1.print(GetdataInt1());            Serial1.print((char)0x4);   // datafield #1
    Serial1.print(GetdataFloat2());          Serial1.print((char)0x5);   // datafield #2
    Serial1.print(displayStatus);                                         // datafield #3
    Serial1.print((char)ETX);                                             // End of Transmission
  }
}

String getButtonStatusString()  {
  String bStatus = "";
  for (int i = 0; i < 6; i++)  {
    if (buttonStatus & (B100000 >> i))      bStatus += "1";
    else                                  bStatus += "0";
  }
  return bStatus;
}

int GetdataInt1()  {              // Data dummy values sent to Android device for demo purpose
  static int i = -30;             // Replace with your own code
  i ++;
  if (i > 0)    i = -30;
  return i;
}

float GetdataFloat2()  {           // Data dummy values sent to Android device for demo purpose
  static float i = 50;             // Replace with your own code
  i -= .5;
  if (i < -50)    i = 50;
  return i;
}

int movementState = 0;

int previousJoyX = 0;
int previousJoyY = 0;
void getJoystickState(byte data[8])    {
  int joyX = (data[1] - 48) * 100 + (data[2] - 48) * 10 + (data[3] - 48); // obtain the Int from the ASCII representation
  int joyY = (data[4] - 48) * 100 + (data[5] - 48) * 10 + (data[6] - 48);
  joyX = joyX - 200;                                                  // Offset to avoid
  joyY = joyY - 200;                                                  // transmitting negative numbers

  // Your code here ...
  Serial.print("Joystick position:  ");
  Serial.print(joyX);
  Serial.print(", ");
  Serial.println(joyY);
  if (joyX < -100 || joyX > 100 || joyY < -100 || joyY > 100)     return; // commmunication error
		

  if (directionAxe) {
    light_turn(joyX);
    if(joyX!=previousJoyX){      
      turn(joyX);
      previousJoyX = joyX;
    }
    if(joyY!=previousJoyY){
      int movement = move(joyY);
      if (movement != movementState) {
        movementState = movement;
        switch (movement) {
          case -1:
            lcd.clear();
            lcd.setCursor(0, 0);
            lcd.print("Backward!");
            break;
          case 0:
            lcd.clear();
            lcd.setCursor(0, 0);
            lcd.print("Stop moving");
            break;
          case 1:
            lcd.clear();
            lcd.setCursor(0, 0);
            lcd.print("Forward!");
            break;
        }
      }
      previousJoyY = joyY;
    }

  } else {
    if (movementState != 2 && (joyX != 0 || joyY != 0)) {
      lcd.setCursor(0, 0);
      lcd.print("Aiming...          ");
      movementState = 2;
    }
    turnTurret(joyX, joyY);
  }
}



void getButtonState(int bStatus)  {
  switch (bStatus) {
    // -----------------  BUTTON #1  -----------------------
    case 'A':
    case 'B':
      buttonStatus |= B000001;        // ON
      Serial.println("\n** FIRE **");
      lcd.clear();
      lcd.setCursor(0, 0);
      lcd.print("Fire !");
      // your code...
      fire();
      displayStatus = "FIRE - " + String(getAmmoLeft()) + " ammo";
      Serial.println(displayStatus);
      lcd.setCursor(0, 1);
      lcd.print(getAmmoStatus());
      break;

    // -----------------  BUTTON #2  -----------------------
    case 'C':
    case 'D':
      buttonStatus |= B000010;        // ON
      Serial.println("\n** Reloading **");
      // your code...
      displayStatus = "Reloading";
      Serial.println(displayStatus);
      reload();
      lcd.clear();
      lcd.setCursor(0, 0);
      lcd.print(displayStatus);
      lcd.setCursor(0, 1);
      lcd.print(getAmmoStatus());
      break;

    // -----------------  BUTTON #3  -----------------------
    case 'E':
      buttonStatus |= B000100;        // ON
      Serial.println("\n** Turret mode Enabled **");
      directionAxe = false;
      displayStatus = "Turret mode Enabled"; // Demo text message
      Serial.println(displayStatus);
      lcd.clear();
      lcd.setCursor(0, 0);
      lcd.print(displayStatus);
      lcd.setCursor(0, 1);
      lcd.print(getAmmoStatus());
      break;
    case 'F':
      buttonStatus &= B111011;      // OFF
      Serial.println("\n** Turret mode Disabled **");
      directionAxe = true;
      // your code...
      displayStatus = "Turret mode Disabled";
      Serial.println(displayStatus);
      lcd.clear();
      lcd.setCursor(0, 0);
      lcd.print(displayStatus);
      break;

    // -----------------  BUTTON #4  -----------------------
    case 'G':
      buttonStatus |= B001000;       // ON
      Serial.println("\n** Lights Front: ON **");
      lightUp(LIGHTS_FRONT, HIGH);
      lightUp(LIGHTS_TOP, HIGH);
      displayStatus = "Lights Front <FAST>";
      Serial.println(displayStatus);
      break;
    case 'H':
      buttonStatus &= B110111;    // OFF
      Serial.println("\n** Lights Front: OFF **");
      lightUp(LIGHTS_FRONT, LOW);
      lightUp(LIGHTS_TOP, LOW);
      displayStatus = "Lights Front <SLOW>";
      Serial.println(displayStatus);
      break;

    // -----------------  BUTTON #5  -----------------------
    case 'I':           // configured as momentary button
      //      buttonStatus |= B010000;        // ON
      Serial.println("\n** Button_5: ++ pushed ++ **");
      // your code...
      displayStatus = "Button5: <pushed>";
      break;
    //   case 'J':
    //     buttonStatus &= B101111;        // OFF
    //     // your code...
    //     break;

    // -----------------  BUTTON #6  -----------------------
    case 'K':
      buttonStatus |= B100000;        // ON
      Serial.println("\n** Lights back: ON **");
      lightUp(LIGHTS_BACK, HIGH);
      displayStatus = "Lights back <ON>"; // Demo text message
      break;
    case 'L':
      buttonStatus &= B011111;        // OFF
      Serial.println("\n** Lights back: OFF **");
      lightUp(LIGHTS_BACK, LOW);
      displayStatus = "Lights back <OFF>";
      break;
  }
  // ---------------------------------------------------------------
}
