# Fritzing sketch Carduino-remote-2020 (saved by Fritzing 0.9.3b)
perfboards: 1

parts:
  Composant1 = Arduino Nano (Rev3.0)
  R1 = Rotary Potentiometer (Small) [maximum_resistance=100kΩ package=THT]
  S1 = Toggle Switch [package=THT]
  LCD1 = LCD screen  # not connected
  J1 = Camdenboss CTB0158-4 [part_number=CTB0158-4 package=THT]
  Composant3 = NRF24L01+ Breakout Board
  U2 = Voltage Regulator -- 3.3 V -- LM1117
  U3 = Voltage Regulator -- 5 V -- LM1117
  R3 = Resistor [tolerance=±5% resistance=100 package="0402 [SMD]"]
  LED1 = smd LED [color="Red (633nm)" package="1206 [SMD]"]
  BAT1 = BC9VPC [package=bc9vpc]
  Composant4 = Black Joystick KY-023

nets:
  GND: Composant1.GND, R1.leg2, S1.COM, J1.pin4, Composant3.GND, U2.GND, U3.GND, LED1.cathode, Composant4.GND
  N1: Composant1.D7, Composant3.CE
  N2: Composant1.D8, Composant3.CS
  N3: Composant1.D11/MOSI, Composant3.MOSI
  N4: Composant1.D12/MISO, Composant3.MISO
  N5: Composant1.VIN, U2.IN, U3.IN, BAT1.V+
  N6: Composant1.A5, J1.pin1
  N7: Composant1.A4, J1.pin2
  N8: Composant1.A3, Composant4.SW
  N9: Composant1.A2, Composant4.VRy
  N10: Composant1.A1, Composant4.VRx
  N11: Composant1.A0, R1.wiper
  N12: Composant1.D13/SCK, Composant3.SCK
  N13: R1.leg1, J1.pin3, U3.OUT, R3.Pin_1, Composant4.+5V
  N14: S1.L1, BAT1.V-
  N15: Composant3.VCC, U2.OUT
  N16: R3.Pin_0, LED1.anode

custom parts:
  Voltage Regulator -- 3.3 V -- LM1117: LM1117-3.3 Voltage regulator, 3.3 V output. Note that the pinout order is not the same as LM7805 or LM7833.
  Voltage Regulator -- 5 V -- LM1117: LM1117-3.3 Voltage regulator, 5 V output. Note that the pinout order is not the same as LM7805 or LM7833.
  Black Joystick KY-023: Description: The joystick is a combination of 2 analoog potentiometer and a digital switch. Arduino GND --> Module pin - Arduino +5V --> Module pin +5V Arduino Analoog 0 --> Module VRx Arduino Analoog 1 --> Module VRy Arduino Digital --> Module SW Dimensions: 1" x 1.25"
